// Logisim project ex5.circ as structural Verilog: 5 circuits, main circuit rotr
module rotr (
  input  [15:0] A,
  input  [3:0] B,
  output [15:0] Out1
);

  wire [15:0] and_1_out, and_2_out, and_3_out, and_4_out, and_5_out, and_6_out, and_7_out, and_8_out,
       bit_extender_1_out, bit_extender_2_out, bit_extender_3_out, bit_extender_4_out, not_1_out, not_2_out,
       not_3_out, not_4_out, or_1_out, or_2_out, or_3_out, rot1_1_out_2, rot2_1_out_2, rot4_1_out_2,
       rot8_1_out_2;

  rot1 rot1_1 (.in_1(A), .out_2(rot1_1_out_2));
  assign bit_extender_1_out = {{15{B[0]}}, B[0]};  // Bit_Extender bit_extender_1
  assign bit_extender_2_out = {{15{B[1]}}, B[1]};  // Bit_Extender bit_extender_2
  assign bit_extender_3_out = {{15{B[2]}}, B[2]};  // Bit_Extender bit_extender_3
  assign bit_extender_4_out = {{15{B[3]}}, B[3]};  // Bit_Extender bit_extender_4
  assign and_1_out = rot1_1_out_2 & bit_extender_1_out;  // AND_Gate and_1, 16 bits wide
  assign and_2_out = A & not_1_out;  // AND_Gate and_2, 16 bits wide
  assign not_1_out = ~bit_extender_1_out;  // NOT_Gate not_1, 16 bits wide
  assign or_1_out = and_1_out | and_2_out;  // OR_Gate or_1, 16 bits wide
  rot2 rot2_1 (.in_1(or_1_out), .out_2(rot2_1_out_2));
  assign not_2_out = ~bit_extender_2_out;  // NOT_Gate not_2, 16 bits wide
  rot4 rot4_1 (.in_1(or_2_out), .out_2(rot4_1_out_2));
  assign not_3_out = ~bit_extender_3_out;  // NOT_Gate not_3, 16 bits wide
  rot8 rot8_1 (.in_1(or_3_out), .out_2(rot8_1_out_2));
  assign not_4_out = ~bit_extender_4_out;  // NOT_Gate not_4, 16 bits wide
  assign and_3_out = rot2_1_out_2 & bit_extender_2_out;  // AND_Gate and_3, 16 bits wide
  assign and_4_out = or_1_out & not_2_out;  // AND_Gate and_4, 16 bits wide
  assign and_5_out = rot4_1_out_2 & bit_extender_3_out;  // AND_Gate and_5, 16 bits wide
  assign and_6_out = or_2_out & not_3_out;  // AND_Gate and_6, 16 bits wide
  assign and_7_out = rot8_1_out_2 & bit_extender_4_out;  // AND_Gate and_7, 16 bits wide
  assign and_8_out = or_3_out & not_4_out;  // AND_Gate and_8, 16 bits wide
  assign or_2_out = and_3_out | and_4_out;  // OR_Gate or_2, 16 bits wide
  assign or_3_out = and_5_out | and_6_out;  // OR_Gate or_3, 16 bits wide
  assign Out1 = and_7_out | and_8_out;  // OR_Gate or_4, 16 bits wide

  // Notes on the sheet:
  //   PUT CIRCUITRY HERE
endmodule

module rot8 (
  input  [15:0] in_1,
  output [15:0] out_2
);


  assign out_2 = {in_1[7:0], in_1[15:8]};

  // Notes on the sheet:
  //   PUT CIRCUITRY HERE
endmodule

module rot4 (
  input  [15:0] in_1,
  output [15:0] out_2
);


  assign out_2 = {in_1[3:0], in_1[15:4]};

  // Notes on the sheet:
  //   PUT CIRCUITRY HERE
endmodule

module rot2 (
  input  [15:0] in_1,
  output [15:0] out_2
);


  assign out_2 = {in_1[1:0], in_1[15:2]};

  // Notes on the sheet:
  //   PUT CIRCUITRY HERE
endmodule

module rot1 (
  input  [15:0] in_1,
  output [15:0] out_2
);


  assign out_2 = {in_1[0], in_1[15:1]};

  // Notes on the sheet:
  //   PUT CIRCUITRY HERE
endmodule
