// Logisim project control_logic.circ as structural Verilog: 1 circuit, main circuit control_logic
module control_logic (
  input  [31:0] inst,
  input  BrEq,
  input  BrLt,
  output PCSel,
  output RegWEn,
  output [2:0] ImmSel,
  output BrUn,
  output ASel,
  output BSel,
  output [3:0] ALUSel,
  output MemRW,
  output [1:0] WBSel,
  output CSRSel,
  output CSRWen
);

  wire and_3_out, and_4_out, and_5_out, and_6_out, and_7_out, and_8_out, and_9_out, and_10_out,
       comparator_1_eq, comparator_2_eq, comparator_9_eq, comparator_10_eq, comparator_14_eq,
       comparator_15_eq, comparator_17_eq, comparator_18_eq, comparator_19_eq, comparator_20_eq,
       comparator_21_eq, comparator_22_eq, comparator_23_eq, comparator_24_eq, comparator_25_lt,
       comparator_26_eq, comparator_27_eq, comparator_28_eq, is_Itype, is_jalr, is_Loadtype, is_Rtype,
       is_SBtype, is_Stype, is_UJtype, is_Utype, not_1_out, not_2_out, not_3_out, or_4_out, or_9_out,
       or_10_out, WBSel_ALUout, WBSel_Imm, WBSel_PC4;
  wire [1:0] multiplexer_4_out, multiplexer_6_out;
  wire [2:0] multiplexer_1_out, multiplexer_2_out, multiplexer_3_out, multiplexer_5_out;
  wire [3:0] multiplexer_9_out, multiplexer_10_out, multiplexer_11_out, multiplexer_12_out,
       multiplexer_13_out, multiplexer_14_out, multiplexer_15_out;

  Comparator #(.width(3)) comparator_1 (.a(inst[14:12]), .b(3'b101), .eq(comparator_1_eq));  // open: gt, lt
  or or_1 (ASel, is_SBtype, is_UJtype, comparator_2_eq);
  Comparator #(.width(7)) comparator_2 (.a(inst[6:0]), .b(7'b0010111), .eq(comparator_2_eq));  // open: gt, lt
  and and_1 (CSRSel, CSRWen, comparator_1_eq);
  Comparator #(.width(7)) comparator_3 (.a(inst[6:0]), .b(7'b0100011), .eq(MemRW));  // open: gt, lt
  Comparator #(.width(7)) comparator_4 (.a(inst[6:0]), .b(7'b0110011), .eq(is_Rtype));  // open: gt, lt
  Comparator #(.width(7)) comparator_5 (.a(inst[6:0]), .b(7'b0000011), .eq(is_Loadtype));  // open: gt, lt
  Comparator #(.width(7)) comparator_6 (.a(inst[6:0]), .b(7'b0010011), .eq(is_Itype));  // open: gt, lt
  Comparator #(.width(7)) comparator_7 (.a(inst[6:0]), .b(7'b0100011), .eq(is_Stype));  // open: gt, lt
  Comparator #(.width(7)) comparator_8 (.a(inst[6:0]), .b(7'b1100011), .eq(is_SBtype));  // open: gt, lt
  Comparator #(.width(7)) comparator_9 (.a(inst[6:0]), .b(7'b0010111), .eq(comparator_9_eq));  // open: gt, lt
  Comparator #(.width(7)) comparator_10 (.a(inst[6:0]), .b(7'b0110111), .eq(comparator_10_eq));  // open: gt, lt
  Comparator #(.width(7)) comparator_11 (.a(inst[6:0]), .b(7'b1101111), .eq(is_UJtype));  // open: gt, lt
  Comparator #(.width(7)) comparator_12 (.a(inst[6:0]), .b(7'b1100111), .eq(is_jalr));  // open: gt, lt
  Comparator #(.width(7)) comparator_13 (.a(inst[6:0]), .b(7'b1110011), .eq(CSRWen));  // open: gt, lt
  Comparator #(.width(3)) comparator_14 (.a(inst[14:12]), .b(3'b110), .eq(comparator_14_eq));  // open: gt, lt
  Comparator #(.width(3)) comparator_15 (.a(inst[14:12]), .b(3'b111), .eq(comparator_15_eq));  // open: gt, lt
  or or_2 (is_Utype, comparator_9_eq, comparator_10_eq);
  or or_3 (RegWEn, is_Rtype, is_jalr, is_Utype, is_UJtype, is_Itype, is_Loadtype);
  and and_2 (BrUn, is_SBtype, or_4_out);
  or or_4 (or_4_out, comparator_14_eq, comparator_15_eq);
  or or_5 (BSel, is_UJtype, is_jalr, is_Itype, is_Stype, is_SBtype, is_Utype, is_Loadtype);
  Comparator #(.width(7)) comparator_16 (.a(inst[6:0]), .b(7'b0110111), .eq(WBSel_Imm));  // open: gt, lt
  Comparator #(.width(7)) comparator_17 (.a(inst[6:0]), .b(7'b0010111), .eq(comparator_17_eq));  // open: gt, lt
  or or_6 (WBSel_PC4, is_jalr, is_UJtype);
  Multiplexer #(.enable("false"), .width(3)) multiplexer_1 (
    .in0(3'b000), .in1(3'b001), .out(multiplexer_1_out), .sel(is_Stype));
  or or_7 (WBSel_ALUout, comparator_17_eq, is_Rtype, is_Itype);
  Multiplexer #(.enable("false"), .width(3)) multiplexer_2 (
    .in0(multiplexer_1_out), .in1(3'b010), .out(multiplexer_2_out), .sel(is_SBtype));
  Multiplexer #(.enable("false"), .width(3)) multiplexer_3 (
    .in0(multiplexer_2_out), .in1(3'b011), .out(multiplexer_3_out), .sel(is_Utype));
  Comparator #(.width(3)) comparator_18 (.a(inst[14:12]), .b(3'b000), .eq(comparator_18_eq));  // open: gt, lt
  Comparator #(.width(3)) comparator_19 (.a(inst[14:12]), .b(3'b001), .eq(comparator_19_eq));  // open: gt, lt
  Comparator #(.width(3)) comparator_20 (.a(inst[14:12]), .b(3'b100), .eq(comparator_20_eq));  // open: gt, lt
  Comparator #(.width(3)) comparator_21 (.a(inst[14:12]), .b(3'b110), .eq(comparator_21_eq));  // open: gt, lt
  Comparator #(.width(3)) comparator_22 (.a(inst[14:12]), .b(3'b101), .eq(comparator_22_eq));  // open: gt, lt
  Comparator #(.width(3)) comparator_23 (.a(inst[14:12]), .b(3'b111), .eq(comparator_23_eq));  // open: gt, lt
  Multiplexer #(.enable("false"), .width(2)) multiplexer_4 (
    .in0(2'b00), .in1(2'b01), .out(multiplexer_4_out), .sel(WBSel_ALUout));
  Multiplexer #(.enable("false"), .width(3)) multiplexer_5 (
    .in0(multiplexer_3_out), .in1(3'b100), .out(multiplexer_5_out), .sel(is_UJtype));
  Comparator #(.width(3)) comparator_24 (.a(inst[14:12]), .b(3'b101), .eq(comparator_24_eq));  // open: gt, lt
  and and_3 (and_3_out, is_SBtype, comparator_18_eq, BrEq);
  and and_4 (and_4_out, is_SBtype, comparator_19_eq, not_1_out);
  not not_1 (not_1_out, BrEq);
  and and_5 (and_5_out, is_SBtype, comparator_20_eq, BrLt);
  and and_6 (and_6_out, is_SBtype, comparator_21_eq, BrLt);
  and and_7 (and_7_out, is_SBtype, comparator_22_eq, not_2_out);
  not not_2 (not_2_out, BrLt);
  and and_8 (and_8_out, is_SBtype, comparator_23_eq, not_3_out);
  not not_3 (not_3_out, is_SBtype);
  Multiplexer #(.enable("false"), .width(2)) multiplexer_6 (
    .in0(multiplexer_4_out), .in1(2'b10), .out(multiplexer_6_out), .sel(WBSel_PC4));
  Multiplexer #(.enable("false"), .width(3)) multiplexer_7 (
    .in0(multiplexer_5_out), .in1(3'b101), .out(ImmSel), .sel(and_9_out));
  and and_9 (and_9_out, CSRWen, comparator_24_eq);
  Multiplexer #(.enable("false"), .width(2)) multiplexer_8 (
    .in0(multiplexer_6_out), .in1(2'b11), .out(WBSel), .sel(WBSel_Imm));
  or or_8 (PCSel, and_3_out, and_4_out, and_5_out, and_6_out, and_7_out, and_8_out, is_UJtype, is_jalr);
  Comparator #(.width(3)) comparator_25 (.a(inst[14:12]), .b(3'b010), .lt(comparator_25_lt));  // open: gt, eq
  Comparator #(.width(7)) comparator_26 (.a(inst[31:25]), .b({7{1'b0}}), .eq(comparator_26_eq));  // open: gt, lt
  Comparator #(.width(7)) comparator_27 (.a(inst[31:25]), .b({7{1'b0}}), .eq(comparator_27_eq));  // open: gt, lt
  Comparator #(.width(7)) comparator_28 (.a(inst[31:25]), .b(7'b0100000), .eq(comparator_28_eq));  // open: gt, lt
  and and_10 (and_10_out, is_SBtype, comparator_25_lt);
  Multiplexer #(.enable("false"), .width(4)) multiplexer_9 (
    .in0(4'b1110), .in1(4'b0110), .out(multiplexer_9_out), .sel(comparator_26_eq));
  Multiplexer #(.enable("false"), .width(4)) multiplexer_10 (
    .in0(4'b0101), .in1(4'b0100), .out(multiplexer_10_out), .sel(comparator_27_eq));
  Multiplexer #(.enable("false"), .width(4)) multiplexer_11 (
    .in0(multiplexer_10_out), .in1(4'b0111), .out(multiplexer_11_out), .sel(is_SBtype));
  Multiplexer #(.enable("false"), .width(4)) multiplexer_12 (
    .in0(4'b0000), .in1(4'b1100), .out(multiplexer_12_out), .sel(or_9_out));
  or or_9 (or_9_out, comparator_28_eq, and_10_out);
  Multiplexer #(.enable("false"), .width(4)) multiplexer_13 (
    .in0(multiplexer_9_out), .in1(4'b1100), .out(multiplexer_13_out), .sel(is_SBtype));
  Multiplexer #(.enable("false"), .width(4)) multiplexer_14 (
    .in0(4'b0011), .in1(4'b0111), .out(multiplexer_14_out), .sel(is_SBtype));
  Multiplexer #(.enable("false"), .select(3), .width(4)) multiplexer_15 (
    .in0(multiplexer_12_out), .in1(multiplexer_13_out), .in2(4'b0111), .in3(4'b1011),
    .in4(multiplexer_14_out), .in5(multiplexer_11_out), .in6(4'b0010), .in7(4'b0001),
    .out(multiplexer_15_out), .sel(inst[14:12]));
  Multiplexer #(.enable("false"), .width(4)) multiplexer_16 (
    .in0(4'b0000), .in1(multiplexer_15_out), .out(ALUSel), .sel(or_10_out));
  or or_10 (or_10_out, is_Itype, is_Rtype);

  // Other names for the same wires on the sheet: opcode[6:0] = inst[6:0]; rd[4:0] = inst[11:7];
  //   func3[2:0] = inst[14:12]; rs1[4:0] = inst[19:15]; rs2[4:0] = inst[24:20]; func7[6:0] = inst[31:25];
  //   is_csrw = CSRWen

  // Notes on the sheet:
  //   INPUTS to your circuit
  //   DON'T CHANGE THE LOCATIONS OF THE INPUTS AND OUTPUTS!
  //   OUTPUT from your circuit
  //   auipc
  //   lui
  //   R
  //   I
  //   jalr
  //   jal
  //   bnq
  //   blt
  //   bltu
  //   bge
  //   bgeu
  //   beq
  //   写回逻辑：立即数、ALU、PC+4
  //   立即数选取逻辑：0 -- 5
  //   PC选择逻辑，选PC+4(0)还是立即数(1)
endmodule
