// Logisim project cpu.circ as structural Verilog: 1 circuit, main circuit cpu
module cpu (
  input  clk,
  input  [31:0] INSTRUCTION,
  input  [31:0] READ_DATA,
  output [31:0] WRITE_ADDRESS,
  output [31:0] PROGRAM_COUNTER,
  output [31:0] ra,
  output [31:0] sp,
  output [31:0] t0,
  output [31:0] t1,
  output [31:0] t2,
  output [31:0] s0,
  output [31:0] s1,
  output [31:0] a0,
  output [31:0] tohost,
  output [3:0] WRITE_ENABLE,
  output [31:0] WRITE_DATA
);

  wire ASel, branch_comp_1_breq, branch_comp_1_brlt, BSel, comparator_1_eq, comparator_2_eq, comparator_3_eq,
       comparator_4_eq, comparator_5_eq, comparator_6_eq, control_logic_1_brun, control_logic_1_csrwen,
       CSRSel, isLB, isLH, isSB, isSH, MemRW, PCSel, RegWEn;
  wire [1:0] WBsel;
  wire [2:0] func3, ImmSel;
  wire [3:0] control_logic_1_alusel, multiplexer_4_out, multiplexer_5_out;
  wire [6:0] func7;
  wire [24:0] INSTRUCTION2;
  wire [31:0] adder_1_out, adder_2_out, bit_extender_1_out, bit_extender_2_out, Imm, multiplexer_1_out,
       multiplexer_2_out, multiplexer_3_out, multiplexer_8_out, multiplexer_10_out, multiplexer_11_out,
       PROGRAM_COUNTER2, r1, READ_DATA2, WB_DATA;

  Adder #(.width(32)) adder_1 (.a(PROGRAM_COUNTER), .b(32'h4), .out(adder_1_out));  // open: cin, cout
  Multiplexer #(.enable("false"), .width(32)) multiplexer_1 (
    .in0(adder_1_out), .in1(WRITE_ADDRESS), .out(multiplexer_1_out), .sel(PCSel));
  and and_1 (isLH, comparator_1_eq, comparator_2_eq);
  Comparator #(.width(3)) comparator_1 (.a(func3), .b(3'b001), .eq(comparator_1_eq));  // open: gt, lt
  Comparator #(.width(7)) comparator_2 (.a(INSTRUCTION2[6:0]), .b(7'b0000011), .eq(comparator_2_eq));  // open: gt, lt
  and and_2 (isLB, comparator_2_eq, comparator_3_eq);
  Comparator #(.width(3)) comparator_3 (.a(func3), .b(3'b000), .eq(comparator_3_eq));  // open: gt, lt
  and and_3 (isSH, comparator_4_eq, comparator_5_eq);
  Comparator #(.width(3)) comparator_4 (.a(func3), .b(3'b001), .eq(comparator_4_eq));  // open: gt, lt
  Comparator #(.width(7)) comparator_5 (.a(INSTRUCTION2[6:0]), .b(7'b0100011), .eq(comparator_5_eq));  // open: gt, lt
  and and_4 (isSB, comparator_5_eq, comparator_6_eq);
  Comparator #(.width(3)) comparator_6 (.a(func3), .b(3'b000), .eq(comparator_6_eq));  // open: gt, lt
  Multiplexer #(.enable("false"), .width(32)) multiplexer_2 (
    .in0(INSTRUCTION), .in1(32'h13), .out(multiplexer_2_out), .sel(PCSel));
  Register #(.width(32)) PC (.D(multiplexer_1_out), .clk(clk), .Q(PROGRAM_COUNTER));  // open: en, clr
  Register #(.width(32)) register_1 (
    .D(multiplexer_2_out), .clk(clk), .Q({func7, INSTRUCTION2[24:15], func3, INSTRUCTION2[11:0]}));  // open: en, clr
  Register #(.width(32)) register_2 (.D(PROGRAM_COUNTER), .clk(clk), .Q(PROGRAM_COUNTER2));  // open: en, clr
  imm_gen imm_gen_1 (.inst({func7, INSTRUCTION2[24:15], func3, INSTRUCTION2[11:0]}), .ImmSel(ImmSel), .imm(Imm));
  control_logic control_logic_1 (
    .CSRWen(control_logic_1_csrwen), .PCSel(PCSel), .RegWEn(RegWEn), .ImmSel(ImmSel),
    .BrUn(control_logic_1_brun), .ASel(ASel), .BSel(BSel), .ALUSel(control_logic_1_alusel), .MemRW(MemRW),
    .WBSel(WBsel), .CSRSel(CSRSel), .inst({func7, INSTRUCTION2[24:15], func3, INSTRUCTION2[11:0]}),
    .BrEq(branch_comp_1_breq), .BrLt(branch_comp_1_brlt));
  assign bit_extender_1_out = {{24{READ_DATA[7]}}, READ_DATA[7:0]};  // Bit_Extender bit_extender_1
  assign bit_extender_2_out = {{16{READ_DATA[15]}}, READ_DATA[15:0]};  // Bit_Extender bit_extender_2
  Multiplexer #(.enable("false"), .width(32)) multiplexer_3 (
    .in0(READ_DATA), .in1(bit_extender_1_out), .out(multiplexer_3_out), .sel(isLB));
  Multiplexer #(.enable("false"), .width(4)) multiplexer_4 (
    .in0(4'b1111), .in1(4'b0011), .out(multiplexer_4_out), .sel(isSH));
  Multiplexer #(.enable("false"), .width(4)) multiplexer_5 (
    .in0(multiplexer_4_out), .in1(4'b0001), .out(multiplexer_5_out), .sel(isSB));
  Multiplexer #(.enable("false"), .width(32)) multiplexer_6 (
    .in0(multiplexer_3_out), .in1(bit_extender_2_out), .out(READ_DATA2), .sel(isLH));
  Multiplexer #(.enable("false"), .width(4)) multiplexer_7 (
    .in0(4'b0000), .in1(multiplexer_5_out), .out(WRITE_ENABLE), .sel(MemRW));
  branch_comp branch_comp_1 (
    .rs1(r1), .rs2(WRITE_DATA), .BrUn(control_logic_1_brun), .BrEq(branch_comp_1_breq),
    .BrLt(branch_comp_1_brlt));
  regfile regfile_1 (
    .rs1(INSTRUCTION2[19:15]), .rs2(INSTRUCTION2[24:20]), .rd(INSTRUCTION2[11:7]), .Write_Data(WB_DATA),
    .RegWEn(RegWEn), .clk(clk), .ra(ra), .sp(sp), .t0(t0), .t1(t1), .t2(t2), .s0(s0), .s1(s1), .a0(a0),
    .Read_Data_1(r1), .Read_Data_2(WRITE_DATA));
  Multiplexer #(.enable("false"), .width(32)) multiplexer_8 (
    .in0(r1), .in1(Imm), .out(multiplexer_8_out), .sel(CSRSel));
  Adder #(.width(32)) adder_2 (.a(PROGRAM_COUNTER2), .b(32'h4), .out(adder_2_out));  // open: cin, cout
  Multiplexer #(.enable("false"), .select(2), .width(32)) multiplexer_9 (
    .in0(READ_DATA2), .in1(WRITE_ADDRESS), .in2(adder_2_out), .in3(Imm), .out(WB_DATA), .sel(WBsel));
  Multiplexer #(.enable("false"), .width(32)) multiplexer_10 (
    .in0(r1), .in1(PROGRAM_COUNTER2), .out(multiplexer_10_out), .sel(ASel));
  Multiplexer #(.enable("false"), .width(32)) multiplexer_11 (
    .in0(WRITE_DATA), .in1(Imm), .out(multiplexer_11_out), .sel(BSel));
  csr csr_1 (
    .CSR_address(12'h51e), .CSR_din(multiplexer_8_out), .CSR_WE(control_logic_1_csrwen), .clk(clk),
    .tohost(tohost));
  alu alu_1 (.Result(WRITE_ADDRESS), .A(multiplexer_10_out), .B(multiplexer_11_out), .ALUSel(control_logic_1_alusel));

  // Other names for the same wires on the sheet: ALUOut[31:0] = WRITE_ADDRESS; opcode[6:0] = INSTRUCTION2[6:0];
  //   rd[4:0] = INSTRUCTION2[11:7]; INSTRUCTION2 (some bits) = {func7, func3}; rs1[4:0] = INSTRUCTION2[19:15];
  //   rs2[4:0] = INSTRUCTION2[24:20]; r2[31:0] = WRITE_DATA

  // Notes on the sheet:
  //   Output to IMEM
  //   IMEM (do **NOT** move this)
  //   Inputs from IMEM
  //   It is OK to move the PC, RegFile, ALU, MEM, Branch Comp, Imm Gen, and Control Logic to wherever is most convenient for you when constructing your CPU, and to delete this text
  //   Inputs/Outputs for testing. Do **NOT** move these.
  //   Outputs To DMEM
  //   DMEM (do **NOT** move this)
  //   Inputs From DMEM
endmodule
